# Fritzing sketch pcb_cistern_sensor (saved by Fritzing 0.9.3b)
breadboards: 1

parts:
  hc-sr1 = hc-sr04  # not connected
  D1 = LED_BARGRAPH_10 [package=led_bargaph_10]
  R1 = Resistor [tolerance=±5% resistance=300 package=THT]
  R2 = Resistor [tolerance=±5% resistance=300 package=THT]
  R3 = Resistor [tolerance=±5% resistance=300 package=THT]
  R4 = Resistor [tolerance=±5% resistance=300 package=THT]
  R5 = Resistor [tolerance=±5% resistance=300 package=THT]
  R6 = Resistor [tolerance=±5% resistance=300 package=THT]
  R7 = Resistor [tolerance=±5% resistance=300 package=THT]
  R8 = Resistor [tolerance=±5% resistance=300 package=THT]
  R9 = Resistor [tolerance=±5% resistance=300 package=THT]
  R10 = Resistor [tolerance=±5% resistance=300 package=THT]
  Part1 = Arduino Nano (Rev3.0)
  IC1 = IC, DIP package, 20 pins [chip_label=IC]  # not connected
  J1 = male pin header, 5 pins [form="♂ (male)"]  # not connected

nets (from the schematic view):
  N1: D1.A_A, Part1.D11/MOSI
  N2: D1.B_A, Part1.D10
  N3: D1.C_A, Part1.D9
  N4: D1.D_A, Part1.D8
  N5: D1.E_A, Part1.D7
  N6: D1.F_A, Part1.D6
  N7: D1.G_A, Part1.D5
  N8: D1.H_A, Part1.D4
  N9: D1.I_A, Part1.D3
  N10: D1.J_A, Part1.D2
  N11: D1.J_C, R10.Pin_0
  N12: D1.I_C, R9.Pin_0
  N13: D1.H_C, R8.Pin_0
  N14: D1.G_C, R7.Pin_0
  N15: D1.F_C, R6.Pin_0
  N16: D1.E_C, R5.Pin_0
  N17: D1.D_C, R4.Pin_0
  N18: D1.C_C, R3.Pin_0
  N19: D1.B_C, R2.Pin_0
  N20: D1.A_C, R1.Pin_0
  N21: R1.Pin_1, R5.Pin_1
  N22: R3.Pin_1, R4.Pin_1, R6.Pin_1, R7.Pin_1, R8.Pin_1, R9.Pin_1, R10.Pin_1, Part1.GND

// code stored in the sketch: cisterna-sensor-code.ino
// ---------------------------------------------------------------------------
// Cistern Sensor - Leandro Lopes - 05/Nov/2017
// Version 1.0
// ---------------------------------------------------------------------------

#include <NewPing.h> //Library to use ultrasonic sensor

#define TRIGGER_PIN  13  // Arduino pin tied to trigger pin on the ultrasonic sensor.
#define ECHO_PIN     12  // Arduino pin tied to echo pin on the ultrasonic sensor.
#define MAX_DISTANCE 200 // Maximum distance we want to ping for (in centimeters). Maximum sensor distance is rated at 400-500cm.

#define EMPTY 170 // Height to measure the capacity when is empty in centimeters
#define FULL 10 // Height to measure the capacity when is full in centimeters

NewPing sonar(TRIGGER_PIN, ECHO_PIN, MAX_DISTANCE); // NewPing setup of pins and maximum distance.

void setup() {
  
  Serial.begin(115200); // Open serial monitor at 115200 baud to see ping results.
  
  //Determines all ports to Bar graph from 2 to 12
  for (int i = 2; i < 12; i++) {
    pinMode(i, OUTPUT);
  }
}

void loop() {
  int distance;  //load distance from ultrasonic sensor
  int level; //level of bar graph to print between 170 (max height - empty) to 10 (min height - full)
  distance = sonar.ping_cm();
  delay(150);                     // Wait 50ms between pings (about 20 pings/sec). 29ms should be the shortest delay between pings.
  level = map(distance, FULL, EMPTY, 0, 10);  //Maps distance to level from 0 to 10
 
  if (distance != 0) {   // Somente ativa se o valor for diferente de 0 
     //If debug on
    Serial.print("Ping: ");
    Serial.print(distance); // Send ping, get distance in cm and print result (0 = outside set distance range)
    Serial.println("cm");
    Serial.println(level);
    
    setbargraph(level);

  }
  

void setbargraph(int level) {
  //Acende somente até o nivel passado na variavel qtde
  for (int i = 0; i < 11; i++) {
     if (i < level) {
        digitalWrite(i+2, LOW);
     }
     else {
        digitalWrite(i+2, HIGH);
     }
  }
}
