# Fritzing sketch pcb_cistern_sensor_v3 (saved by Fritzing 0.9.3b)
circuit board: 6.25866cm x 4.69425cm
breadboards: 3

parts:
  Part2 = Arduino Nano (Rev3.0)
  hc-sr1 = hc-sr04
  D1 = LED_BARGRAPH_10 [package=led_bargaph_10]
  R1 = Resistor [tolerance=±5% resistance=300 package=THT]
  R2 = Resistor [tolerance=±5% resistance=300 package=THT]
  R3 = Resistor [tolerance=±5% resistance=300 package=THT]
  R4 = Resistor [tolerance=±5% resistance=300 package=THT]
  R5 = Resistor [tolerance=±5% resistance=300 package=THT]
  R6 = Resistor [tolerance=±5% resistance=300 package=THT]
  R7 = Resistor [tolerance=±5% resistance=300 package=THT]
  R8 = Resistor [tolerance=±5% resistance=300 package=THT]
  R9 = Resistor [tolerance=±5% resistance=300 package=THT]
  R10 = Resistor [tolerance=±5% resistance=300 package=THT]
  VCC1 = Battery block 9V

nets:
  GND: Part2.GND, hc-sr1.GND, R1.Pin_0, R2.Pin_0, R3.Pin_0, R4.Pin_0, R5.Pin_0, R6.Pin_0, R7.Pin_0, R8.Pin_0, R9.Pin_0, R10.Pin_0, VCC1.-
  N1: Part2.D2, D1.A_C
  N2: Part2.D3, D1.B_C
  N3: Part2.D4, D1.C_C
  N4: Part2.D5, D1.D_C
  N5: Part2.D6, D1.E_C
  N6: Part2.D7, D1.F_C
  N7: Part2.D8, D1.G_C
  N8: Part2.D9, D1.H_C
  N9: Part2.D10, D1.I_C
  N10: Part2.D11/MOSI, D1.J_C
  N11: Part2.D12/MISO, hc-sr1.Echo
  N12: Part2.VIN, VCC1.+
  5V: Part2.5V, hc-sr1.VCC
  N13: Part2.D13/SCK, hc-sr1.Trig
  N14: D1.A_A, R1.Pin_1
  N15: D1.B_A, R2.Pin_1
  N16: D1.C_A, R3.Pin_1
  N17: D1.D_A, R4.Pin_1
  N18: D1.E_A, R5.Pin_1
  N19: D1.F_A, R6.Pin_1
  N20: D1.G_A, R7.Pin_1
  N21: D1.H_A, R8.Pin_1
  N22: D1.I_A, R9.Pin_1
  N23: D1.J_A, R10.Pin_1
